# Fritzing sketch smartbutton (saved by Fritzing 0.9.3b)
breadboards: 1

parts:
  부품1 = SRF05 Ultrasonic Rangefinder
  M1 = >Wemos D1 R32
  DFRobot_DFPlayer_Mini1 = DFRobot DFPlayer Mini [part_number=DFR0299]
  SP1 = SPEAKER [package=pcb_mount_speaker]
  BUTTON1 = Arcade Button (white)
  R1 = PHOTOCELL [package=photocell-kit]
  R2 = Resistor [tolerance=±5% resistance=220 package="1206 [SMD]"]
  DHT2 = DHT11 Humitidy and Temperature Sensor (3 pins)
  LED1 = LED - 3mm [color="Red (633nm)" package="3 mm [THT]"]
  R3 = Resistor [tolerance=±5% resistance=220 package="1206 [SMD]"]
  R4 = Resistor [tolerance=±5% resistance=220 package="1206 [SMD]"]

nets:
  VCC: 부품1.VCC, M1.5V, BUTTON1.no_name_yet#1, R2.Pin_0, DHT2.DATA
  N1: 부품1.Trig, M1.IO12
  N2: 부품1.Echo, M1.IO13
  GND: 부품1.GND, M1.GND, DFRobot_DFPlayer_Mini1.BUSY, R1.P$1, DHT2.GND, LED1.cathode, R4.Pin_1
  N3: M1.IO4, DHT2.VDD
  N4: M1.IO39, R1.P$2, R2.Pin_1
  N5: M1.IO19, BUTTON1.no_name_yet#2, R4.Pin_0
  N6: M1.IO18, DFRobot_DFPlayer_Mini1.GND-1, DFRobot_DFPlayer_Mini1.GND-2, R3.Pin_1
  N7: DFRobot_DFPlayer_Mini1.IO_1, SP1.-
  N8: LED1.anode, R3.Pin_0

custom parts:
  >Wemos D1 R32: Wemos D1 R32 - This board is used with dual-mode Wi-Fi and Bluetooth chips, which is safe, reliable, and scalable to a variety of applications. DC in 5V-12V, 1 analog input(3.2V max input), a Micro USB connection, Compatible with D1 R32=WiFi+bluetooth+UNO
  Arcade Button (white): Adafruit Arcade Button (white)
  DHT11 Humitidy and Temperature Sensor (3 pins): DHT11 Humidity and Temperature Sensor (3 pins) from the design created by John De Cristofaro for Adafruit Industries.
